# Fritzing sketch equilibrista (saved by Fritzing 0.9.10b)
perfboards: 1

parts:
  U3 = LuaNode32 / ESP32
  IC2 = Voltage Regulator [package=78xxl]
  DC_Mot_Enc3 = DC Motor with two-phase hall-encoder [part_number=VT-E-G25A-06-177E]  # not connected
  DC_Mot_Enc4 = DC Motor with two-phase hall-encoder [part_number=VT-E-G25A-06-177E]  # not connected
  Componente7 = NRF24L01+ Breakout Board
  Componente8 = InvenSense MPU6050
  U4 = LIPO-1000mAh [package=lipo-1000]  # not connected
  S2 = Toggle Switch [package=THT]
  R2 = Resistor [tolerance=±5% resistance=220 package="2010 [SMD]"]  # not connected
  LED5 = LED - 5mm [color="Red (633nm)" current=0.030 package="5 mm [THT]"]  # not connected
  TRM12 = Terminal 2pin
  TRM13 = Terminal 2pin
  TRM14 = Borne kre 2 vias
  TRM15 = Borne kre 2 vias
  TRM16 = Borne kre 2 vias
  TRM17 = Borne kre 2 vias
  TRM18 = Borne kre 2 vias
  Componente9 = Motor Driver 1A Dual TB6612FNG
  D2 = P1000K [part_number=P1000K]  # not connected
  J2 = Dagu DGServo 9g header (male) [package=THT]  # not connected
  U5 = LM2596 step down module
  J3 = Piezo Speaker

nets:
  N1: U3.VP, TRM13.pin_2
  N2: U3.VN, TRM13.pin_1
  N3: U3.D34, TRM12.pin_2
  N4: U3.D35, TRM12.pin_1
  N5: U3.D33, Componente9.PWMA
  N6: U3.D25, Componente9.AIN2
  N7: U3.D26, Componente9.AIN1
  N8: U3.D27, Componente9.STBY
  N9: U3.D14, Componente9.BIN1
  N10: U3.D12, Componente9.BIN2
  N11: U3.D13, Componente9.PWMB
  GND: U3.GND, Componente7.GND, Componente8.GND, Componente9.GND
  N12: U3.Vin, IC2.OUT
  3V3: U3.3V3, Componente8.VCC
  N13: U3.D4, J3.pin2
  N14: U3.D5, Componente7.CE
  N15: U3.D18, Componente7.SCK
  N16: U3.D19, Componente7.MISO
  N17: U3.D21, Componente8.SDA
  N18: U3.RX0, Componente7.IRQ
  N19: U3.TX0, Componente7.CS
  N20: U3.D22, Componente8.SCL
  N21: U3.D23, Componente7.MOSI
  N22: IC2.GND, TRM16.pin_1, TRM17.pin_2, U5.IN-, U5.OUT-
  N23: IC2.IN, S2.L1
  N24: S2.COM, TRM16.pin_2
  N25: TRM14.pin_1, Componente9.B01
  N26: TRM14.pin_2, TRM18.pin_1, Componente9.VCC
  N27: TRM15.pin_2, Componente9.B02
  N28: TRM17.pin_1, Componente9.A02
  N29: TRM18.pin_2, Componente9.A01
  N30: Componente9.VM, U5.OUT+

custom parts:
  LuaNode32 / ESP32: ESP32 based LuaNode32
  Terminal 2pin: 2-pin Terminal Block
  Borne kre 2 vias: 2-pin Terminal Block
  LM2596 step down module: LM2596 DC-DC step down power supply module 3 A.
